# Fritzing sketch full-module (saved by Fritzing 0.9.9b)

parts:
  M1 = DOIT Esp32 DevKit v1 (30 pins long, 11 pins width) [part_number=ESP32S-PIN30]
  Part3 = RFID-RC522-v3
  HC-SR04_Sensor_2 = HC-SR04 Ultrasonic Distance Sensor

nets:
  3V3: M1.3V3, Part3.3.3V
  GND: M1.GND, Part3.GND, HC-SR04_Sensor_2.GND
  N1: M1.D2, HC-SR04_Sensor_2.TRIG
  N2: M1.D4, HC-SR04_Sensor_2.ECHO
  N3: M1.D18, Part3.SCK
  N4: M1.D19, Part3.MISO
  N5: M1.D21, Part3.SDA
  N6: M1.D22, Part3.RST
  N7: M1.D23, Part3.MOSI
  VIN: M1.VIN, HC-SR04_Sensor_2.VCC

notes:
  HC-SR04: Vcc and Gnd must be connected with VIN and GND

custom parts:
  DOIT Esp32 DevKit v1 (30 pins long, 11 pins width): The DOIT Esp32 DevKit v1 is one of the development board created by DOIT to evaluate the ESP-WROOM-32 module. It is based on the ESP32 microcontroller that boasts Wifi, Bluetooth, Ethernet and Low Power support all in a single chip. (vanepp) made breadboard work, adjusted pin numbering and labels and reduced size of schematic and cleaned up pcb. This chip is 30pins long (2 x15) and 11 pins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
  RFID-RC522-v3: A simple China made RFID-RC522 Reader (6x4 cm); do check the pin labels, as this is a MFRC522 based clone.
